// Logisim project gol_16.circ as structural Verilog: 6 circuits, main circuit gol16
module gol16 (
);

  wire aadd, and_1_out, anop, aop, asub, ccoe, clk, clr, coe, ctrue, frce, froe, ibread, ibwrite, iclk, irce,
       iroe, lroe, marce, maroe, mdrce, mdrget, mdroe, mdrput, pcoe, rd, regr, regw, rx, ry, si7, si9, spoe,
       t1ce, t1oe, t2ce, t2oe, ui4, ui7, ui9;
  wire [1:0] reg16_1_q_2;
  wire [2:0] controlled_buffer_1_out;
  wire [3:0] alu_1_c, cc, reg4_1_q;
  wire [3:2] reg16_1_q_3;
  wire [4:0] multiplexer_1_out, OpBus;
  wire [15:0] alu_1_r, controlled_buffer_9_out, controlled_buffer_19_out, controlled_buffer_21_out, mar_q,
       mdr_q, reg16_1_q, reg16_2_q;

  Button button_1 (.out(clr));
  Clock clock_1 (.out(clk));
  assign controlled_buffer_1_out[1:0] = rd ? reg16_1_q_3 : 2'bz;  // Controlled_Buffer controlled_buffer_1
  assign OpBus = aop ? reg16_1_q[15:11] : 5'bz;  // Controlled_Buffer controlled_buffer_2
  not not_1 (iclk, clk);
  assign controlled_buffer_1_out[1:0] = rx ? reg16_1_q_2 : 2'bz;  // Controlled_Buffer controlled_buffer_3
  assign controlled_buffer_1_out = pcoe ? 3'b100 : 3'bz;  // Controlled_Buffer controlled_buffer_4
  assign controlled_buffer_1_out[1:0] = ry ? reg16_1_q[6:5] : 2'bz;  // Controlled_Buffer controlled_buffer_5
  assign cc = ccoe ? {reg16_1_q_3, reg16_1_q_2} : 4'bz;  // Controlled_Buffer controlled_buffer_6
  and and_1 (and_1_out, ~reg16_1_q[15], reg16_1_q[14], ~reg16_1_q[13], ~reg16_1_q[12], ~reg16_1_q[11]);  // AND_Gate
  assign OpBus = aop ? multiplexer_1_out : 5'bz;  // Controlled_Buffer controlled_buffer_7
  Multiplexer #(.enable("true"), .select(2), .width(5)) multiplexer_1 (
    .in0(5'b01000), .in1(5'b01010), .in2(5'b01011), .in3(5'b01100), .out(multiplexer_1_out), .en(and_1_out));  // open: sel
  fsm fsm_1 (.OP(reg16_1_q[15:11]), .CLK(clr), .CLR(clk), .cTrue(ctrue));  // open: signals
  assign controlled_buffer_1_out = spoe ? 3'b101 : 3'bz;  // Controlled_Buffer controlled_buffer_8
  assign controlled_buffer_9_out = ui7 ? {{9{1'b0}}, reg16_1_q[6:0]} : 16'bz;  // Controlled_Buffer controlled_buffer_9
  assign controlled_buffer_1_out = lroe ? 3'b110 : 3'bz;  // Controlled_Buffer controlled_buffer_10
  assign controlled_buffer_9_out = ui9 ? {{7{1'b0}}, reg16_1_q_2, reg16_1_q[6:0]} : 16'bz;  // Controlled_Buffer controlled_buffer_11
  assign controlled_buffer_9_out = ui4 ? {{12{1'b0}}, reg16_1_q[3:0]} : 16'bz;  // Controlled_Buffer controlled_buffer_12
  assign OpBus = aadd ? 5'b00001 : 5'bz;  // Controlled_Buffer controlled_buffer_13
  assign OpBus = anop ? {5{1'b0}} : 5'bz;  // Controlled_Buffer controlled_buffer_14
  assign OpBus = asub ? 5'b00010 : 5'bz;  // Controlled_Buffer controlled_buffer_15
  assign controlled_buffer_9_out = si7 ? {{10{reg16_1_q[6]}}, reg16_1_q[5:0]} : 16'bz;  // Controlled_Buffer controlled_buffer_16
  assign controlled_buffer_9_out = si9 ? {{8{reg16_1_q_2[1]}}, reg16_1_q_2[0], reg16_1_q[6:0]} : 16'bz;  // Controlled_Buffer controlled_buffer_17
  reg16 reg16_1 (
    .OE(iroe), .CE(irce), .CLK(iclk), .D(controlled_buffer_9_out), .CLR(clr),
    .Q({reg16_1_q[15:11], reg16_1_q_3, reg16_1_q_2, reg16_1_q[6:0]}));
  RAM #(.addrWidth(3), .dataWidth(16)) registers (
    .addr(controlled_buffer_1_out), .we(regw), .oe(regr), .clk(iclk), .din(controlled_buffer_9_out),
    .dout(controlled_buffer_9_out));
  assign controlled_buffer_9_out = coe ? 16'h1 : 16'bz;  // Controlled_Buffer controlled_buffer_18
  reg16 reg16_2 (.OE(t1oe), .CE(t1ce), .CLK(iclk), .D(controlled_buffer_9_out), .CLR(clr), .Q(reg16_2_q));
  alu alu_1 (
    .Op(OpBus[3:0]), .A(reg16_2_q), .Z(alu_1_c[3]), .C(alu_1_c[0]), .V(alu_1_c[1]), .N(alu_1_c[2]),
    .R(alu_1_r));  // open: B
  reg16 reg16_3 (.OE(t2oe), .CE(t2ce), .CLK(iclk), .D(alu_1_r), .CLR(clr), .Q(controlled_buffer_9_out));
  reg4 reg4_1 (.OE(froe), .CE(frce), .CLK(iclk), .D(alu_1_c), .CLR(clr), .Q(reg4_1_q));
  ccEval cceval_1 (.cc(cc), .cTrue(ctrue), .C(reg4_1_q[0]), .V(reg4_1_q[1]), .N(reg4_1_q[2]), .Z(reg4_1_q[3]));
  assign controlled_buffer_19_out = mdrput ? controlled_buffer_9_out : 16'bz;  // Controlled_Buffer controlled_buffer_19
  assign controlled_buffer_9_out = mdrget ? mdr_q : 16'bz;  // Controlled_Buffer controlled_buffer_20
  reg16 mdr (.OE(mdroe), .CE(mdrce), .CLK(iclk), .D(controlled_buffer_19_out), .CLR(clr), .Q(mdr_q));
  assign controlled_buffer_21_out = ibwrite ? mdr_q : 16'bz;  // Controlled_Buffer controlled_buffer_21
  assign controlled_buffer_19_out = ibread ? controlled_buffer_21_out : 16'bz;  // Controlled_Buffer controlled_buffer_22
  reg16 mar (.OE(maroe), .CE(marce), .CLK(iclk), .D(controlled_buffer_9_out), .CLR(clr), .Q(mar_q));
  RAM #(.addrWidth(16), .dataWidth(16)) ram_1 (
    .addr(mar_q), .we(ibwrite), .oe(ibread), .clk(iclk), .din(controlled_buffer_21_out),
    .dout(controlled_buffer_21_out));
  // also tied to GND on the sheet: controlled_buffer_1_out[2]

  // Notes on the sheet:
  //   Detect shift/rotate op
endmodule

module alu (
  input  [3:0] Op,
  input  [15:0] A,
  input  [15:0] B,
  output [15:0] R,
  output Z,
  output C,
  output V,
  output N
);

  wire addc, or_3_out, or_4_out, seventeen_out, subb, zero_out;
  wire [2:0] divf, mulf;
  wire [2:1] addf, subf;
  wire [4:0] bitadder_1_out;
  wire [7:0] divq, divrem;
  wire [14:0] addr, divr, mulr, subr;
  wire [15:0] and_1_out, mulc, mulv, not_1_out, or_1_out, shifter_1_out, shifter_2_out, shifter_3_out,
       shifter_4_out;

  Multiplier #(.mode("twosComplement"), .width(16)) multiplier_1 (.a(A), .b(B), .cout(mulv));  // open: out, cin
  xor xor_1 (addf[1], addc, addf[2]);
  xor xor_2 (subf[1], subb, subf[2]);
  Adder #(.width(16)) adder_1 (.a(A), .b(B), .out({addf[2], addr}), .cin(1'b0), .cout(addc));
  Subtractor #(.width(16)) subtractor_1 (.a(B), .b(B), .out({subf[2], subr}), .bin(1'b0), .bout(subb));
  Multiplier #(.width(16)) multiplier_2 (.a(A), .b(B), .out({mulf[2], mulr}), .cout(mulc));  // open: cin
  Divider #(.width(16)) divider_1 (
    .a(A), .b(B), .out({divq, divr[7:0]}), .rem({divrem, divf[2], divr[14:8]}));  // open: upper
  assign and_1_out = A & B;  // AND_Gate and_1, 16 bits wide
  assign or_1_out = A | B;  // OR_Gate or_1, 16 bits wide
  assign not_1_out = ~B;  // NOT_Gate not_1, 16 bits wide
  Shifter #(.width(16)) shifter_1 (.in(A), .\dist (B[3:0]), .out(shifter_1_out));
  Shifter #(.shift("lr"), .width(16)) shifter_2 (.in(A), .\dist (B[3:0]), .out(shifter_2_out));
  Shifter #(.shift("rl"), .width(16)) shifter_3 (.in(A), .\dist (B[3:0]), .out(shifter_3_out));
  Shifter #(.shift("rr"), .width(16)) shifter_4 (.in(A), .\dist (B[3:0]), .out(shifter_4_out));
  BitAdder #(.width(17)) bitadder_1 (.in0({mulv, mulf[2]}), .out(bitadder_1_out));
  or or_2 (mulf[0], mulc[7], mulc[0], mulc[1], mulc[2], mulc[3], mulc[4], mulc[5], mulc[6], mulc[8], mulc[9], mulc[10], mulc[11], mulc[12], mulc[13], mulc[14], mulc[15]);
  and seventeen (seventeen_out, bitadder_1_out[0], ~bitadder_1_out[1], ~bitadder_1_out[2], ~bitadder_1_out[3], bitadder_1_out[4]);  // AND_Gate
  nor zero (zero_out, bitadder_1_out[0], bitadder_1_out[1], bitadder_1_out[2], bitadder_1_out[3], bitadder_1_out[4]);
  nor nor_1 (mulf[1], seventeen_out, zero_out);
  Multiplexer #(.select(4), .width(16)) multiplexer_1 (
    .in0({16{1'b0}}), .in1({addf[2], addr}), .in2({subf[2], subr}), .in3({mulf[2], mulr}),
    .in4({divf[2], divr}), .in5(and_1_out), .in6(or_1_out), .in7(not_1_out), .in8(shifter_1_out), .in9(B),
    .in10(shifter_2_out), .in11(shifter_3_out), .in12(shifter_4_out), .out(R), .sel(Op));  // open: in13, in14, in15
  or or_3 (or_3_out, divq[3], divq[0], divq[1], divq[2], divq[4], divq[5], divq[6], divq[7]);
  or or_4 (or_4_out, divrem[3], divrem[0], divrem[1], divrem[2], divrem[4], divrem[5], divrem[6], divrem[7]);
  or or_5 (divf[0], or_3_out, or_4_out);
  Multiplexer #(.select(4), .width(3)) multiplexer_2 (
    .in0(3'b000), .in1({addf, addc}), .in2({subf, subb}), .in3(mulf), .in4({divf[2], 1'b0, divf[0]}),
    .in5(3'b000), .in6(3'b000), .in7(3'b000), .in8(3'b000), .in9(3'b000), .in10(3'b000), .in11(3'b000),
    .out({N, V, C}), .sel(Op));  // open: in12, in13, in14, in15
  nor nor_2 (Z, R[15], R[14], R[13], R[12], R[11], R[10], R[9], R[8], R[7], R[6], R[5], R[4], R[3], R[2], R[1], R[0]);

  // Other names for the same wires on the sheet: addf[0] = addc; addr[15] = addf[2]; divr[15] = divf[2];
  //   mulr[15] = mulf[2]; oper[3:0] = Op; subf[0] = subb; subr[15] = subf[2]

  // Notes on the sheet:
  //   Single source operations use B
  //   Add flag generator
  //   Sub flag generator
  //   Detects if any of the 2's compliment multiplication bits + the MSB of the result are different (XOR)
  //   Logisim XOR used voting behaviour which was not desirable
  //   8b remainder 8b quotient, remainder stored in MSBs
  //   Multiplication flag generator
  //   No operation
  //   Division flag generator
  //   Result MUX
  //   Signed division can be implemented in software by correcting for (negating output appropriately) the signs of the two operands
  //   Due to the complexity of signed division, this ALU will only perform unsigned division (hence 0 for V flag)
  //   Flag MUX
endmodule

module reg16 (
  input  [15:0] D,
  input  CE,
  input  OE,
  input  CLK,
  input  CLR,
  output [15:0] Q
);

  wire [15:0] register_1_q;

  Register #(.width(16)) register_1 (.D(D), .en(CE), .clk(CLK), .Q(register_1_q), .clr(CLR));
  assign Q = OE ? register_1_q : 16'bz;  // Controlled_Buffer controlled_buffer_1
endmodule

// FR
module reg4 (
  input  [3:0] D,
  input  CE,
  input  OE,
  input  CLK,
  input  CLR,
  output [3:0] Q
);

  wire [3:0] register_1_q;

  Register #(.width(4)) register_1 (.D(D), .en(CE), .clk(CLK), .Q(register_1_q), .clr(CLR));
  assign Q = OE ? register_1_q : 4'bz;  // Controlled_Buffer controlled_buffer_1
endmodule

module fsm (
  input  CLK,
  input  CLR,
  input  [4:0] OP,
  input  [29:0] signals,
  input  cTrue
);

  wire branch_out, BranchOp_out, decode_state_out;
  wire [7:0] decode_data, multiplexer_1_out, multiplexer_2_out, register_1_q;
  wire [63:0] fsm_data;

  ROM #(.addrWidth(5)) decode (.addr(OP), .data(decode_data));
  Multiplexer #(.width(8)) multiplexer_1 (
    .in0(fsm_data[7:0]), .in1(decode_data), .out(multiplexer_1_out), .sel(decode_state_out));
  Multiplexer #(.width(8)) multiplexer_2 (
    .in0(multiplexer_1_out), .in1({8{1'b0}}), .out(multiplexer_2_out), .sel(branch_out));
  and branch (branch_out, BranchOp_out, cTrue);
  and BranchOp (BranchOp_out, OP[0], OP[1], OP[2], OP[3]);
  and decode_state (decode_state_out, fsm_data[0], fsm_data[1], ~fsm_data[2], ~fsm_data[3], ~fsm_data[4], ~fsm_data[5], ~fsm_data[6], ~fsm_data[7]);  // AND_Gate
  Register register_1 (.D(multiplexer_2_out), .en(CLK), .clk(CLK), .Q(register_1_q), .clr(CLR));
  ROM #(.dataWidth(64)) fsm (.addr(register_1_q), .data({fsm_data[63:38], signals, fsm_data[7:0]}));

  // Notes on the sheet:
  //   State F0
  //   contents of fsm (hex, n*v repeats v):
  //   210018081 8c44000202 5090000003 14100 10008885 20009246 10004500 10008888 20400246 20008a06 10804400
  //   20800206 1000848d 8008840 1000848f 8800040 6000251 210000112 8c10000013 5010004400 10008895 4009251
  //   10008897 5000251 6000259 21000011a 281000841b 11410000000 1000889d 4009259 1000889f 5000259 6000246
  //   10082022 5000263 10014100 10082025 10044122
endmodule

module ccEval (
  input  C,
  input  V,
  input  N,
  input  Z,
  input  cTrue,
  input  [3:0] cc
);

  wire ge, gt, hi, le, lo, ls, lt, ne, pl, vc;

  not not_1 (lo, C);
  not not_2 (pl, N);
  not not_3 (vc, V);
  not not_4 (ne, Z);
  and and_1 (hi, C, ~Z);  // AND_Gate
  or or_1 (ls, ~C, Z);  // OR_Gate
  xnor xnor_1 (ge, N, V);
  not not_5 (lt, ge);
  and and_2 (gt, ge, ~Z);  // AND_Gate
  and and_3 (le, lt, Z);
  Multiplexer #(.select(4)) multiplexer_1 (
    .in1(Z), .in2(ne), .in3(C), .in4(hi), .in5(lo), .in6(ls), .in7(N), .in8(pl), .in9(V), .in10(vc),
    .in11(ge), .in12(lt), .in13(gt), .in14(le), .in15(1'b1), .out(cTrue));  // open: in0, sel

  // Other names for the same wires on the sheet: eq = Z; hs = C; mi = N; vs = V

  // Notes on the sheet:
  //   al
endmodule
